// Logisim project setha_tristan_comp306_a1_8_bit_ALU.circ as structural Verilog: 12 circuits, main circuit main
module main (
  input  [7:0] A,
  input  [7:0] B,
  input  Enable_Control_Unit,
  input  [2:0] Opcode,
  input  Shift,
  input  Cin,
  input  [1:0] Cmp,
  output [7:0] Result,
  output Zero,
  output Negative,
  output Carry_out,
  output Overflow
);

  wire comparator_1_eq, comparator_1_gt, comparator_1_lt, control_unit_1_add_sub, control_unit_1_andor,
       control_unit_1_incdec, control_unit_1_shiftdir_2, or_1_out;
  wire [0:0] multiplexer_2_out;
  wire [1:0] control_unit_1_compareop;
  wire [2:0] control_unit_1_aluop;
  wire [7:0] increment_1_out_3, multiplexer_1_out, multiplexer_3_out, n8_bit_adder_subtracter_1_result,
       n8_bit_and_1_out_3, n8_bit_or_1_out_3, n8_bitwise_not_1_out_2, register_left_logic_shift_1_out_2,
       register_right_logic_shift_1_out_2;

  Control_Unit control_unit_1 (
    .E(Enable_Control_Unit), .Opcode(Opcode), .ShiftDir(Shift), .Cin(Cin), .Cmp(Cmp),
    .ALUOp(control_unit_1_aluop), .ShiftDir_2(control_unit_1_shiftdir_2), .AndOr(control_unit_1_andor),
    .Add_Sub(control_unit_1_add_sub), .IncDec(control_unit_1_incdec), .CompareOp(control_unit_1_compareop));  // open: NOT
  Register_left_logic_shift register_left_logic_shift_1 (.in_1(A), .out_2(register_left_logic_shift_1_out_2));
  Register_right_logic_shift register_right_logic_shift_1 (.in_1(A), .out_2(register_right_logic_shift_1_out_2));
  _8_bitwise_NOT u_8_bitwise_not_1 (.in_1(A), .out_2(n8_bitwise_not_1_out_2));
  _8_bit_AND u_8_bit_and_1 (.in_1(A), .in_2(B), .out_3(n8_bit_and_1_out_3));
  _8_bit_OR u_8_bit_or_1 (.out_3(n8_bit_or_1_out_3), .in_1(A), .in_2(B));
  _8_bit_Adder_Subtracter u_8_bit_adder_subtracter_1 (
    .Add_Subtract_Control(control_unit_1_add_sub), .Result(n8_bit_adder_subtracter_1_result),
    .Carry_out(Carry_out), .Overflow(Overflow), .A(A), .B(B));
  Increment increment_1 (
    .in_2(A), .out_3(increment_1_out_3), .out_4(Carry_out), .out_5(Overflow), .in_1(control_unit_1_incdec));
  Comparator comparator_1 (.a(A), .b(B), .gt(comparator_1_gt), .eq(comparator_1_eq), .lt(comparator_1_lt));
  Multiplexer #(.width(8)) multiplexer_1 (
    .in0(register_left_logic_shift_1_out_2), .in1(register_right_logic_shift_1_out_2),
    .out(multiplexer_1_out), .sel(control_unit_1_shiftdir_2));  // open: en
  Multiplexer #(.select(2)) multiplexer_2 (
    .in0(comparator_1_gt), .in1(comparator_1_eq), .in2(comparator_1_lt), .out(multiplexer_2_out[0]),
    .sel(control_unit_1_compareop));  // open: in3, en
  Multiplexer #(.width(8)) multiplexer_3 (
    .in0(n8_bit_and_1_out_3), .in1(n8_bit_or_1_out_3), .out(multiplexer_3_out), .sel(control_unit_1_andor));  // open: en
  Multiplexer #(.select(3), .width(8)) multiplexer_4 (
    .in0(multiplexer_1_out), .in1(n8_bitwise_not_1_out_2), .in2(multiplexer_3_out),
    .in3(n8_bit_adder_subtracter_1_result), .in4(increment_1_out_3), .in5({{7{1'b0}}, multiplexer_2_out[0]}),
    .out({Negative, Result[6:0]}), .sel(control_unit_1_aluop));  // open: in6, in7, en
  or or_1 (or_1_out, Result[0], Result[1], Result[2], Result[3], Result[4], Result[5], Result[6], Negative);
  not not_1 (Zero, or_1_out);

  assign Result[7] = Negative;
endmodule

module Half_adder (
  input  in_1,
  input  in_2,
  output out_3,
  output out_4
);

  xor xor_1 (out_3, in_1, in_2);
  and and_1 (out_4, in_1, in_2);
endmodule

module Full_Adder (
  input  Cin,
  input  A,
  input  B,
  output Sum,
  output Cout
);

  wire HA_1_out_3, HA_1_out_4, HA_2_out_4;

  Half_adder HA_1 (.in_1(A), .in_2(B), .out_3(HA_1_out_3), .out_4(HA_1_out_4));
  Half_adder HA_2 (.in_1(Cin), .in_2(HA_1_out_3), .out_3(Sum), .out_4(HA_2_out_4));
  or or_1 (Cout, HA_2_out_4, HA_1_out_4);
endmodule

module _8_bit_Adder_Subtracter (
  input  Add_Subtract_Control,
  input  [7:0] A,
  input  [7:0] B,
  output [7:0] Result,
  output Carry_out,
  output Overflow
);

  wire and_1_out, and_2_out, full_adder_1_cout, full_adder_2_cout, full_adder_3_cout, full_adder_4_cout,
       full_adder_5_cout, full_adder_6_cout, full_adder_7_cout, not_1_out, not_2_out, not_3_out, xor_1_out,
       xor_2_out, xor_3_out, xor_4_out, xor_5_out, xor_6_out, xor_7_out, xor_8_out;

  xor xor_1 (xor_1_out, Add_Subtract_Control, B[0]);
  xor xor_2 (xor_2_out, Add_Subtract_Control, B[1]);
  xor xor_3 (xor_3_out, Add_Subtract_Control, B[2]);
  xor xor_4 (xor_4_out, Add_Subtract_Control, B[3]);
  xor xor_5 (xor_5_out, Add_Subtract_Control, B[4]);
  xor xor_6 (xor_6_out, Add_Subtract_Control, B[5]);
  xor xor_7 (xor_7_out, Add_Subtract_Control, B[6]);
  xor xor_8 (xor_8_out, Add_Subtract_Control, B[7]);
  not not_1 (not_1_out, A[7]);
  not not_2 (not_2_out, xor_8_out);
  Full_Adder full_adder_1 (
    .Cin(Add_Subtract_Control), .A(A[0]), .B(xor_1_out), .Sum(Result[0]), .Cout(full_adder_1_cout));
  Full_Adder full_adder_2 (.Cin(full_adder_1_cout), .A(A[1]), .B(xor_2_out), .Sum(Result[1]), .Cout(full_adder_2_cout));
  Full_Adder full_adder_3 (.Cin(full_adder_2_cout), .A(A[2]), .B(xor_3_out), .Sum(Result[2]), .Cout(full_adder_3_cout));
  Full_Adder full_adder_4 (.Cin(full_adder_3_cout), .A(A[3]), .B(xor_4_out), .Sum(Result[3]), .Cout(full_adder_4_cout));
  Full_Adder full_adder_5 (.Cin(full_adder_4_cout), .A(A[4]), .B(xor_5_out), .Sum(Result[4]), .Cout(full_adder_5_cout));
  Full_Adder full_adder_6 (.Cin(full_adder_5_cout), .A(A[5]), .B(xor_6_out), .Sum(Result[5]), .Cout(full_adder_6_cout));
  Full_Adder full_adder_7 (.Cin(full_adder_6_cout), .A(A[6]), .B(xor_7_out), .Sum(Result[6]), .Cout(full_adder_7_cout));
  Full_Adder full_adder_8 (.Cin(full_adder_7_cout), .A(A[7]), .B(xor_8_out), .Sum(Result[7]), .Cout(Carry_out));
  not not_3 (not_3_out, Result[7]);
  and and_1 (and_1_out, Result[7], not_1_out, not_2_out);
  and and_2 (and_2_out, not_3_out, A[7], xor_8_out);
  or or_1 (Overflow, and_1_out, and_2_out);
endmodule

module _8_bit_AND (
  input  [7:0] in_1,
  input  [7:0] in_2,
  output [7:0] out_3
);

  and and_1 (out_3[0], in_1[0], in_2[0]);
  and and_2 (out_3[1], in_1[1], in_2[1]);
  and and_3 (out_3[2], in_1[2], in_2[2]);
  and and_4 (out_3[3], in_1[3], in_2[3]);
  and and_5 (out_3[4], in_1[4], in_2[4]);
  and and_6 (out_3[5], in_1[5], in_2[5]);
  and and_7 (out_3[6], in_1[6], in_2[6]);
  and and_8 (out_3[7], in_1[7], in_2[7]);
endmodule

module _8_bit_OR (
  input  [7:0] in_1,
  input  [7:0] in_2,
  output [7:0] out_3
);

  or or_1 (out_3[0], in_1[0], in_2[0]);
  or or_2 (out_3[1], in_1[1], in_2[1]);
  or or_3 (out_3[2], in_1[2], in_2[2]);
  or or_4 (out_3[3], in_1[3], in_2[3]);
  or or_5 (out_3[4], in_1[4], in_2[4]);
  or or_6 (out_3[5], in_1[5], in_2[5]);
  or or_7 (out_3[6], in_1[6], in_2[6]);
  or or_8 (out_3[7], in_1[7], in_2[7]);
endmodule

module neso_full_adder (
  input  a,
  input  b,
  input  ci,
  output out_4
);

  wire xor_1_out;

  xor xor_1 (xor_1_out, a, b);
  xor xor_2 (out_4, xor_1_out, ci);
endmodule

module Increment (
  input  in_1,
  input  [7:0] in_2,
  output [7:0] out_3,
  output out_4,
  output out_5
);

  _8_bit_Adder_Subtracter u_8_bit_adder_subtracter_1 (
    .Add_Subtract_Control(in_1), .Result(out_3), .Carry_out(out_4), .Overflow(out_5), .A(in_2), .B(8'h1));
endmodule

module _8_bitwise_NOT (
  input  [7:0] in_1,
  output [7:0] out_2
);

  not not_1 (out_2[0], in_1[0]);
  not not_2 (out_2[1], in_1[1]);
  not not_3 (out_2[2], in_1[2]);
  not not_4 (out_2[3], in_1[3]);
  not not_5 (out_2[4], in_1[4]);
  not not_6 (out_2[5], in_1[5]);
  not not_7 (out_2[6], in_1[6]);
  not not_8 (out_2[7], in_1[7]);
endmodule

module Register_right_logic_shift (
  input  [7:0] in_1,
  output [7:0] out_2
);


  assign out_2 = {1'b0, in_1[7:1]};
endmodule

module Register_left_logic_shift (
  input  [7:0] in_1,
  output [7:0] out_2
);


  assign out_2 = {in_1[6:0], 1'b0};
endmodule

module Control_Unit (
  input  E,
  input  [2:0] Opcode,
  input  ShiftDir,
  input  Cin,
  input  [1:0] Cmp,
  output [2:0] ALUOp,
  output ShiftDir_2,
  output NOT,
  output AndOr,
  output Add_Sub,
  output IncDec,
  output [1:0] CompareOp
);

  wire decoder_1_out0, decoder_1_out2, decoder_1_out3, decoder_1_out4, decoder_1_out5;

  Decoder #(.select(3)) decoder_1 (
    .out0(decoder_1_out0), .out1(NOT), .out2(decoder_1_out2), .out3(decoder_1_out3), .out4(decoder_1_out4),
    .out5(decoder_1_out5), .sel(Opcode), .en(E));  // open: out6, out7
  and and_1 (ShiftDir_2, decoder_1_out0, ShiftDir);
  and and_2 (AndOr, decoder_1_out2, Cin);
  and and_3 (Add_Sub, decoder_1_out3, Cin);
  and and_4 (IncDec, decoder_1_out4, Cin);
  and and_5 (CompareOp[0], decoder_1_out5, Cmp[0]);
  and and_6 (CompareOp[1], decoder_1_out5, Cmp[1]);

  assign ALUOp = Opcode;
endmodule
